# Fritzing sketch схема электрическая (saved by Fritzing 0.9.3b)

parts:
  U0 = Arduino Mega 2560 (Rev3)
  M_Link_1 = Stepper Motor - Bipolar
  M_Link_0 = Stepper Motor - Bipolar
  M_Link_2 = Stepper Motor - Bipolar
  M_Load_0 = Basic Servo
  M_Link_4 = Basic Servo
  M_Link_5 = Basic Servo
  M_Link_3 = Basic Servo
  V1 = DC Power [voltage=5V]
  V2 = DC Power [voltage=12V]
  V3 = DC Power [voltage=5V]
  S1 = SPST Switch [package=switche-dpdt]
  U1 = EasyDriver_v44
  U2 = EasyDriver_v44
  U3 = L298_BRIDGE_DRIVER [package=powerso20]

nets:
  GND: U0.GND, M_Link_4.gnd, M_Link_3.gnd, S1.P, U1.GND, U2.GND
  N1: U0.D12_PWM, M_Load_0.pulse
  N2: U0.D10_PWM, M_Link_5.pulse
  N3: U0.D9_PWM, M_Link_4.pulse
  N4: U0.D8_PWM, M_Link_3.pulse
  N5: U0.5V, V1.V+
  N6: U0.D33, U1.DIR
  N7: U0.D35, U1.ENABLE
  N8: U0.D37, U3.IN1
  N9: U0.D39, U3.IN2
  N10: U0.D41, U3.IN3
  N11: U0.D43, U3.IN4
  N12: U0.D45, U1.STEP
  N13: U0.D47, U1.PFD
  N14: U0.D49, U2.STEP
  N15: U0.D51, U2.DIR
  N16: U0.D53, U2.ENABLE
  N17: M_Link_1.A, U2.OUT1A
  N18: M_Link_1.C, U2.OUT2A
  N19: M_Link_1.B, U2.OUT1B
  N20: M_Link_1.D, U2.OUT2B
  N21: M_Link_0.A, U3.OUT4
  N22: M_Link_0.C, U3.OUT3
  N23: M_Link_0.B, U3.OUT1
  N24: M_Link_0.D, U3.OUT2
  N25: M_Link_2.A, U1.OUT1A
  N26: M_Link_2.C, U1.OUT2A
  N27: M_Link_2.B, U1.OUT1B
  N28: M_Link_2.D, U1.OUT2B
  GND_2: M_Load_0.gnd, M_Link_5.gnd
  VCC: M_Load_0.vcc, M_Link_4.vcc, M_Link_5.vcc, M_Link_3.vcc, V3.V+
  N29: V1.V-, V2.V-, V3.V-, S1.S
  VCC_2: V2.V+, U1.VCC, U2.VCC, U3.VS
